# Fritzing sketch master-slave (saved by Fritzing 0.9.5d)
breadboards: 2

parts:
  U2 = NodeMCU V1.0
  R3 = Photocell (LDR) [package=THT]
  LED1 = LED - 5mm [color="Green (555nm)" package="5 mm [THT]"]
  R6 = Resistor [tolerance=±5% resistance=10k package=THT]
  R7 = Resistor [tolerance=±5% resistance=200 package=THT]
  U3 = NodeMCU V1.0
  R8 = Photocell (LDR) [package=THT]
  LED2 = LED - 5mm [color="Green (555nm)" package="5 mm [THT]"]
  R9 = Resistor [tolerance=±5% resistance=10k package=THT]
  R10 = Resistor [tolerance=±5% resistance=200 package=THT]
  Componente4 = LCD1602-I2C
  IR_Receiver4 = IR_Receiver
  SERVO4 = Tower Pro SG90 servo [part_number=101246]

nets:
  N1: U2.D1, LED1.cathode
  N2: U2.3V3, R7.Pin_1
  N3: U2.GND, R3.pin_1
  N4: U2.TX, U2.A0, R6.Pin_0
  N5: U2.RST, U3.D7
  N6: R3.pin_0, R6.Pin_1
  N7: LED1.anode, R7.Pin_0
  N8: U3.D1, Componente4.SCL
  N9: U3.D2, Componente4.SDA
  N10: U3.D3, IR_Receiver4.OUT
  3V3: U3.3V3, R8.pin_1, R10.Pin_0, IR_Receiver4.VCC
  GND: U3.GND, U3.A0, R9.Pin_0, Componente4.GND, IR_Receiver4.GND, SERVO4.GND
  N11: U3.D5, LED2.cathode
  N12: U3.D6, SERVO4.Signal
  VIN: U3.Vin, Componente4.VCC, SERVO4.+5V
  N13: R8.pin_0, R9.Pin_1
  N14: LED2.anode, R10.Pin_1

custom parts:
  NodeMCU V1.0: ESP8266 based NodeMCU
  LCD1602-I2C: A standard character display, usually with 2x16 characters. Comes in many colors with LCM1602 IIC attached.
  IR_Receiver: 赤外線受信モジュール GP1UXC41QS
  Tower Pro SG90 servo: Original file by John De Cristofaro http://www.adafruit.com/products/1449 Adafruit Feedback Servo (Small) Edited by: e-radionica.com 28/9/2015
